# Fritzing sketch S3X_Proxy (saved by Fritzing 0.9.3b)
breadboards: 1

parts:
  U1 = ESP8266 ESP-01 Upgraded WiFi Module [part_number=ESP8266]
  元件2 = DC-DC Power Module (3.3v)
  U3 = RS485 [package=so08]
  R1 = Resistor [tolerance=±5% resistance=220 package=THT]
  LED1 = LED - 5mm [color="Red (633nm)" package="5 mm [THT]"]
  LED2 = LED - 5mm [color="Green (570nm)" package="5 mm [THT]"]
  U4 = USB_AB [package=usb-ab-micro-smd]
  R2 = Resistor [tolerance=±5% resistance=220 package=THT]

nets:
  N1: U1.RXD, U3.RO
  N2: U1.GPIO_0, LED1.anode
  N3: U1.GPIO_2, LED2.anode
  VIN: 元件2.Vin, U3.GND, U3.A, R1.Pin_0, U4.VBUS, R2.Pin_0
  GND: 元件2.GND, LED2.cathode, U4.GND, R2.Pin_1
  N4: R1.Pin_1, LED1.cathode

custom parts:
  ESP8266 ESP-01 Upgraded WiFi Module: Upgraded Version ESP-01,all Flash are upgraded to 1M byte.Also support Cloud service remote transmission.
  DC-DC Power Module (3.3v): DC-DC Power Module based con AMS1117-3.3 Input: DC 4.5~7V (input power must higher 1V than output power); Output: 3.3V (+/-0.05V error), 800mA
